# Fritzing sketch LC-Relay-ESP-32-4R-A2 (saved by Fritzing 1.0.8)
breadboards: 1

parts:
  Bauteil1 = ESP-WROOM-32 [ESP-32S] Module [part_number=ESP-WROOM-32]
  VR1 = LM2596 (TO263) [part_number=LM2596 package=TO263]
  U2 = AMS1117 Voltage Regulator
  J3 = Camdenboss CTB0158-3 [part_number=CTB0158-3 package=THT]
  J1 = double row male pin header, 20 pins [form="♂ (male)"]
  J2 = double row male pin header, 20 pins [form="♂ (male)"]
  P5 = male pin header, 6 pins [form="♂ (male)"]
  C1 = Electrolytic Capacitor [capacitance=220µF voltage=50V package="100 mil [THT, electrolytic]"]
  D1 = smd LED [color="Red (633nm)" current=0.030A package="0603 [SMD]"]
  D5 = smd LED [color="Red (633nm)" current=0.030A package="0603 [SMD]"]
  D9 = smd LED [color="Red (633nm)" current=0.030A package="0603 [SMD]"]
  D11 = smd LED [color="Red (633nm)" current=0.030A package="0603 [SMD]"]
  R28 = Resistor [tolerance=±5% resistance=10k power=0.25W package="0603 [SMD]"]
  C14 = Ceramic Capacitor [capacitance=100nF voltage=35V package="0603 [SMD, multilayer]"]
  RY1 = srd-05vdc-sl-c
  J4 = Camdenboss CTB0158-3 [part_number=CTB0158-3 package=THT]
  Q1 = TRANSISTOR_NPN [package=sot23]
  R8 = Resistor [tolerance=±5% resistance=1k power=0.25W package="0603 [SMD]"]
  R7 = Resistor [tolerance=±5% resistance=4.7k power=0.25W package="0603 [SMD]"]
  R9 = Resistor [tolerance=±5% resistance=10k power=0.25W package="0603 [SMD]"]
  D3 = Rectifier Diode [package="Melf DO-213 AA [SMD]"]
  R6 = Resistor [tolerance=±5% resistance=100 power=0.25W package="1206 [SMD]"]
  C3 = Ceramic Capacitor [capacitance=100µF voltage=35V package="1206 [SMD, multilayer]"]
  RY2 = srd-05vdc-sl-c
  J5 = Camdenboss CTB0158-3 [part_number=CTB0158-3 package=THT]
  Q2 = TRANSISTOR_NPN [package=sot23]
  R15 = Resistor [tolerance=±5% resistance=1k power=0.25W package="0603 [SMD]"]
  R14 = Resistor [tolerance=±5% resistance=4.7k power=0.25W package="0603 [SMD]"]
  R16 = Resistor [tolerance=±5% resistance=10k power=0.25W package="0603 [SMD]"]
  D6 = Rectifier Diode [package="Melf DO-213 AA [SMD]"]
  R13 = Resistor [tolerance=±5% resistance=100 power=0.25W package="1206 [SMD]"]
  C6 = Ceramic Capacitor [capacitance=100µF voltage=35V package="1206 [SMD, multilayer]"]
  RY3 = srd-05vdc-sl-c
  J6 = Camdenboss CTB0158-3 [part_number=CTB0158-3 package=THT]
  Q3 = TRANSISTOR_NPN [package=sot23]
  R19 = Resistor [tolerance=±5% resistance=1k power=0.25W package="0603 [SMD]"]
  R18 = Resistor [tolerance=±5% resistance=4.7k power=0.25W package="0603 [SMD]"]
  R20 = Resistor [tolerance=±5% resistance=10k power=0.25W package="0603 [SMD]"]
  D10 = Rectifier Diode [package="Melf DO-213 AA [SMD]"]
  R17 = Resistor [tolerance=±5% resistance=100 power=0.25W package="1206 [SMD]"]
  C9 = Ceramic Capacitor [capacitance=100µF voltage=35V package="1206 [SMD, multilayer]"]
  RY4 = srd-05vdc-sl-c
  J7 = Camdenboss CTB0158-3 [part_number=CTB0158-3 package=THT]
  Q4 = TRANSISTOR_NPN [package=sot23]
  R24 = Resistor [tolerance=±5% resistance=1k power=0.25W package="0603 [SMD]"]
  R23 = Resistor [tolerance=±5% resistance=4.7k power=0.25W package="0603 [SMD]"]
  R27 = Resistor [tolerance=±5% resistance=10k power=0.25W package="0603 [SMD]"]
  D12 = Rectifier Diode [package="Melf DO-213 AA [SMD]"]
  R22 = Resistor [tolerance=±5% resistance=100 power=0.25W package="1206 [SMD]"]
  C13 = Ceramic Capacitor [capacitance=100µF voltage=35V package="1206 [SMD, multilayer]"]
  C10 = Ceramic Capacitor [capacitance=100nF voltage=35V package="0603 [SMD, multilayer]"]
  C11 = Ceramic Capacitor [capacitance=100nF voltage=35V package="0603 [SMD, multilayer]"]
  C12 = Ceramic Capacitor [capacitance=100nF voltage=35V package="0603 [SMD, multilayer]"]
  D13 = smd LED [color="Red (633nm)" current=0.030A package="0603 [SMD]"]
  D14 = smd LED [color="Red (633nm)" current=0.030A package="0603 [SMD]"]
  R21 = Resistor [tolerance=±5% resistance=4.7k power=0.25W package="0603 [SMD]"]
  R26 = Resistor [tolerance=±5% resistance=1k power=0.25W package="0603 [SMD]"]
  IOO = Pushbutton [package=THT]
  EN = Pushbutton [package=THT]
  R25 = Resistor [tolerance=±5% resistance=10k power=0.25W package="0603 [SMD]"]
  C15 = Electrolytic Capacitor [capacitance=220µF voltage=50V package="100 mil [THT, electrolytic]"]
  L1 = Inductor [package="1206 [SMD]"]
  D15 = Schottky Diode [part_number=1N5817 package="Melf DO-213 AB [SMD]"]

nets:
  N1: Bauteil1.GND#0, J1.pin20, P5.pin4, P5.pin5
  N2: Bauteil1.3V3, J1.pin1, R28.Pin_0
  N3: Bauteil1.EN, J1.pin19, R28.Pin_1, C14.1, EN.leg0
  N4: Bauteil1.SVP, J1.pin2
  N5: Bauteil1.SVN, J1.pin18
  N6: Bauteil1.IO34, J1.pin3
  N7: Bauteil1.IO35, J1.pin17
  N8: Bauteil1.IO32, J1.pin4, R8.Pin_1
  N9: Bauteil1.IO33, J1.pin16, R15.Pin_1
  N10: Bauteil1.IO25, J1.pin5, R19.Pin_1
  N11: Bauteil1.IO26, J1.pin15, R24.Pin_1
  N12: Bauteil1.IO27, J1.pin6
  N13: Bauteil1.IO14, J1.pin14
  N14: Bauteil1.IO12, J1.pin7
  N15: Bauteil1.IO13, J1.pin13
  N16: Bauteil1.SD2, J1.pin8
  N17: Bauteil1.SD3, J1.pin12
  N18: Bauteil1.GND#51, J2.pin1
  N19: Bauteil1.CLK, J2.pin10
  N20: Bauteil1.SD0, J2.pin12
  N21: Bauteil1.SD1, J2.pin9
  N22: Bauteil1.IO15, J2.pin13
  N23: Bauteil1.IO2, J2.pin8
  N24: Bauteil1.IO0, J2.pin14, P5.pin6, IOO.leg0, R25.Pin_1
  N25: Bauteil1.IO4, J2.pin7
  N26: Bauteil1.IO16, J2.pin15
  N27: Bauteil1.IO17, J2.pin6
  N28: Bauteil1.IO5, J2.pin16
  N29: Bauteil1.IO18, J2.pin5
  N30: Bauteil1.IO19, J2.pin17
  N31: Bauteil1.IO20, J2.pin4
  N32: Bauteil1.IO21, J2.pin18
  N33: Bauteil1.RXD0, J2.pin3, P5.pin3
  N34: Bauteil1.TXD0, J2.pin19, P5.pin2
  N35: Bauteil1.IO22, J2.pin2
  N36: Bauteil1.IO23, J2.pin20, D14.cathode
  N37: VR1.Pin_1, J3.pin1, C15.+
  N38: VR1.Pin_2, L1.pin_0, D15.cathode
  GND: VR1.Pin_3, VR1.Pin_5, VR1.Tab, U2.GND, J3.pin2, C1.-, Q1.E, R9.Pin_1, Q2.E, R16.Pin_1, Q3.E, R20.Pin_1, Q4.E, R27.Pin_1, C10.0, C11.0, C12.0, D13.cathode, IOO.leg1, EN.leg1, C15.-, D15.anode
  N39: VR1.pin_4, J1.pin11, P5.pin1, C1.+, L1.pin_1
  N40: U2.VOUT, J2.pin11, C11.1, C12.1, R25.Pin_0
  N41: U2.VIN, J3.pin3, D1.cathode, D5.cathode, D9.cathode, D11.cathode, RY1.pin_4, D3.cathode, C3.0, RY2.pin_4, D6.cathode, C6.0, RY3.pin_4, D10.cathode, C9.0, RY4.pin_4, D12.cathode, C13.0, C10.1, R21.Pin_1, R26.Pin_1
  N42: D1.anode, R7.Pin_0
  N43: D5.anode, R14.Pin_0
  N44: D9.anode, R18.Pin_0
  N45: D11.anode, R23.Pin_0
  N46: RY1.pin_1, Q1.C, R7.Pin_1, D3.anode, R6.Pin_0
  N47: RY1.pin_2, J4.pin3
  N48: RY1.pin_3, J4.pin1
  N49: RY1.pin_5, J4.pin2
  N50: Q1.B, R8.Pin_0, R9.Pin_0
  N51: R6.Pin_1, C3.1
  N52: RY2.pin_1, Q2.C, R14.Pin_1, D6.anode, R13.Pin_0
  N53: RY2.pin_2, J5.pin3
  N54: RY2.pin_3, J5.pin1
  N55: RY2.pin_5, J5.pin2
  N56: Q2.B, R15.Pin_0, R16.Pin_0
  N57: R13.Pin_1, C6.1
  N58: RY3.pin_1, Q3.C, R18.Pin_1, D10.anode, R17.Pin_0
  N59: RY3.pin_2, J6.pin3
  N60: RY3.pin_3, J6.pin1
  N61: RY3.pin_5, J6.pin2
  N62: Q3.B, R19.Pin_0, R20.Pin_0
  N63: R17.Pin_1, C9.1
  N64: RY4.pin_1, Q4.C, R23.Pin_1, D12.anode, R22.Pin_0
  N65: RY4.pin_2, J7.pin3
  N66: RY4.pin_3, J7.pin1
  N67: RY4.pin_5, J7.pin2
  N68: Q4.B, R24.Pin_0, R27.Pin_0
  N69: R22.Pin_1, C13.1
  N70: D13.anode, D14.anode, R21.Pin_0, R26.Pin_0

notes:
  5V
  TXD0
  RXD0
  GND
  IO0

custom parts:
  ESP-WROOM-32 [ESP-32S] Module: Espressif ESP-WROOM-32 WiFi/Bluetooth LE microcontroller module also known as the Ai-Thinker ESP-32S module with similar formfactor. The ESP32 is a microcontroller chip with WiFi and BLE capabilities. The chip is developed by Espressif and is the successor to the popular ESP8266 WiFi module.
